// Logisim project cntmv.circ as structural Verilog: 1 circuit, main circuit cntmv
module cntmv (
  input  [10:0] in_1,
  output [11:0] out_2
);

  ROM #(.addrWidth(11), .dataWidth(12)) rom_1 (.addr(in_1), .data(out_2));  // open: sel

  // Notes on the sheet:
  //   contents of rom_1 (hex, n*v repeats v):
  //   187 fe a7 c4 1a4 95 84 eb fd 1c7 1d5 1e5 db 1b9 1b6 1f6 1f9 1b5 fb c3 1a3 83 1ca 88 99 96 aa bb c8
  //   cc dd ed e2 ee ff 1a8 1d6 d2 192 1d9 1e6 1e9 1f5 b2 1a1 c1 81 f2 1b2 181 a1 1c1 1f2 1e2 92 1d2 b5
  //   1fb 183 1c3 a3 1c8 a8 ca d6 d9 e6 e9 f5 c7 e5 188 87 d5 f9 184 a4 f6 195 196 199 1a7 b6 1aa b9 91
  //   1bb 1c4 1cc 1d1 1db 1dd 1e1 1eb 1ed 1ee 1fd 1fe 1ff 1b1 182 1c2 a2 c9 86 c6 98 da ea f7 1a6 1a9 1b4
  //   1d8 1dc 1e3 93 1d3 b7 1e8 1ec 1f1 1f3 1cb ba 1f4 1b8 1e4 1b3 d7 85 94 e7 c5 fa f3 197 1a5 1d4 b8 cb
  //   1ba 1f8 97 e4 b3 a5 fc 185 d4 f8 a6 d8 a9 dc e8 f4 ec 186 194 e3 b4 198 1b7 1c5 d3 193 1c6 1c9 1d7
  //   1da 1e7 b1 1ea 1f7 1fa 1fc c2 f1 1a2 82 d1 191 e1 187 fe a7 c4 1a4 95 84 eb fd 1c7 1d5 1e5 db 1b9
  //   1b6 1f6 1f9 1b5 fb c3 1a3 83 1ca 88 99 96 aa bb c8 cc dd ed e2 ee ff 1a8 1d6 d2 192 1d9 1e6 1e9 1f5
  //   b2 1a1 c1 81 f2 1b2 181 a1 1c1 1f2 1e2 92 1d2 b5 1fb 183 1c3 a3 1c8 a8 ca d6 d9 e6 e9 f5 c7 e5 188
  //   87 d5 f9 184 a4 f6 195 196 199 1a7 b6 1aa b9 91 1bb 1c4 1cc 1d1 1db 1dd 1e1 1eb 1ed 1ee 1fd 1fe 1ff
  //   1b1 182 1c2 a2 c9 86 c6 98 da ea f7 1a6 1a9 1b4 1d8 1dc 1e3 93 1d3 b7 1e8 1ec 1f1 1f3 1cb ba 1f4 1b8
  //   1e4 1b3 d7 85 94 e7 c5 fa f3 197 1a5 1d4 b8 cb 1ba 1f8 97 e4 b3 a5 fc 185 d4 f8 a6 d8 a9 dc e8 f4 ec
  //   186 194 e3 b4 198 1b7 1c5 d3 193 1c6 1c9 1d7 1da 1e7 b1 1ea 1f7 1fa 1fc c2 f1 1a2 82 d1 191 e1 187
  //   fe a7 c4 1a4 95 84 eb fd 1c7 1d5 1e5 db 1b9 1b6 1f6 1f9 1b5 fb c3 1a3 83 1ca 88 99 96 aa bb c8 cc dd
  //   ed e2 ee ff 1a8 1d6 d2 192 1d9 1e6 1e9 1f5 b2 1a1 c1 81 f2 1b2 181 a1 1c1 1f2 1e2 92 1d2 b5 1fb 183
  //   1c3 a3 1c8 a8 ca d6 d9 e6 e9 f5 c7 e5 188 87 d5 f9 184 a4 f6 195 196 199 1a7 b6 1aa b9 91 1bb 1c4
  //   1cc 1d1 1db 1dd 1e1 1eb 1ed 1ee 1fd 1fe 1ff 1b1 182 1c2 a2 c9 86 c6 98 da ea f7 1a6 1a9 1b4 1d8 1dc
  //   1e3 93 1d3 b7 1e8 1ec 1f1 1f3 1cb ba 1f4 1b8 1e4 1b3 d7 85 94 e7 c5 fa f3 197 1a5 1d4 b8 cb 1ba 1f8
  //   97 e4 b3 a5 fc 185 d4 f8 a6 d8 a9 dc e8 f4 ec 186 194 e3 b4 198 1b7 1c5 d3 193 1c6 1c9 1d7 1da 1e7
  //   b1 1ea 1f7 1fa 1fc c2 f1 1a2 82 d1 191 e1 187 fe a7 c4 1a4 95 84 eb fd 1c7 1d5 1e5 db 1b9 1b6 1f6
  //   1f9 1b5 fb c3 1a3 83 1ca 88 99 96 aa bb c8 cc dd ed e2 ee ff 1a8 1d6 d2 192 1d9 1e6 1e9 1f5 b2 1a1
  //   c1 81 f2 1b2 181 a1 1c1 1f2 1e2 92 1d2 b5 1fb 183 1c3 a3 1c8 a8 ca d6 d9 e6 e9 f5 c7 e5 188 87 d5 f9
  //   184 a4 f6 195 196 199 1a7 b6 1aa b9 91 1bb 1c4 1cc 1d1 1db 1dd 1e1 1eb 1ed 1ee 1fd 1fe 1ff 1b1 182
  //   1c2 a2 c9 86 c6 98 da ea f7 1a6 1a9 1b4 1d8 1dc 1e3 93 1d3 b7 1e8 1ec 1f1 1f3 1cb ba 1f4 1b8 1e4 1b3
  //   d7 85 94 e7 c5 fa f3 197 1a5 1d4 b8 cb 1ba 1f8 97 e4 b3 a5 fc 185 d4 f8 a6 d8 a9 dc e8 f4 ec 186 194
  //   e3 b4 198 1b7 1c5 d3 193 1c6 1c9 1d7 1da 1e7 b1 1ea 1f7 1fa 1fc c2 f1 1a2 82 d1 191 e1 187 fe a7 c4
  //   1a4 95 84 eb fd 1c7 1d5 1e5 db 1b9 1b6 1f6 1f9 1b5 fb c3 1a3 83 1ca 88 99 96 aa bb c8 cc dd ed e2 ee
  //   ff 1a8 1d6 d2 192 1d9 1e6 1e9 1f5 b2 1a1 c1 81 f2 1b2 181 a1 1c1 1f2 1e2 92 1d2 b5 1fb 183 1c3 a3
  //   1c8 a8 ca d6 d9 e6 e9 f5 c7 e5 188 87 d5 f9 184 a4 f6 195 196 199 1a7 b6 1aa b9 91 1bb 1c4 1cc 1d1
  //   1db 1dd 1e1 1eb 1ed 1ee 1fd 1fe 1ff 1b1 182 1c2 a2 c9 86 c6 98 da ea f7 1a6 1a9 1b4 1d8 1dc 1e3 93
  //   1d3 b7 1e8 1ec 1f1 1f3 1cb ba 1f4 1b8 1e4 1b3 d7 85 94 e7 c5 fa f3 197 1a5 1d4 b8 cb 1ba 1f8 97 e4
  //   b3 a5 fc 185 d4 f8 a6 d8 a9 dc e8 f4 ec 186 194 e3 b4 198 1b7 1c5 d3 193 1c6 1c9 1d7 1da 1e7 b1 1ea
  //   1f7 1fa 1fc c2 f1 1a2 82 d1 191 e1 187 fe a7 c4 1a4 95 84 eb fd 1c7 1d5 1e5 db 1b9 1b6 1f6 1f9 1b5
  //   fb c3 1a3 83 1ca 88 99 96 aa bb c8 cc dd ed e2 ee ff 1a8 1d6 d2 192 1d9 1e6 1e9 1f5 b2 1a1 c1 81 f2
  //   1b2 181 a1 1c1 1f2 1e2 92 1d2 b5 1fb 183 1c3 a3 1c8 a8 ca d6 d9 e6 e9 f5 c7 e5 188 87 d5 f9 184 a4
  //   f6 195 196 199 1a7 b6 1aa b9 91 1bb 1c4 1cc 1d1 1db 1dd 1e1 1eb 1ed 1ee 1fd 1fe 1ff 1b1 182 1c2 a2
  //   c9 86 c6 98 da ea f7 1a6 1a9 1b4 1d8 1dc 1e3 93 1d3 b7 1e8 1ec 1f1 1f3 1cb ba 1f4 1b8 1e4 1b3 d7 85
  //   94 e7 c5 fa f3 197 1a5 1d4 b8 cb 1ba 1f8 97 e4 b3 a5 fc 185 d4 f8 a6 d8 a9 dc e8 f4 ec 186 194 e3 b4
  //   198 1b7 1c5 d3 193 1c6 1c9 1d7 1da 1e7 b1 1ea 1f7 1fa 1fc c2 f1 1a2 82 d1 191 e1 187 fe a7 c4 1a4 95
  //   84 eb fd 1c7 1d5 1e5 db 1b9 1b6 1f6 1f9 1b5 fb c3 1a3 83 1ca 88 99 96 aa bb c8 cc dd ed e2 ee ff 1a8
  //   1d6 d2 192 1d9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
endmodule
