// Logisim project grDeltaMem.circ as structural Verilog: 1 circuit, main circuit grnDeltaMem
module grnDeltaMem (
  input  [5:0] in_1,
  output [23:0] out_2
);

  ROM #(.addrWidth(6), .dataWidth(24)) rom_1 (.addr(in_1), .data(out_2));  // open: sel

  // Notes on the sheet:
  //   contents of rom_1 (hex, n*v repeats v):
  //   6261d9 21 2101f 4001d 14b01f 16a01e 188020 1a8014 5d01e 7b01e 9901e b701d d401e f201d 10f01e 12d01e
  //   1bc01d 2d601f 2f501f 314021 335021 35601f 37501f 394020 3b401f 3d301f 3f201f 1d901e 41101e 42f01f
  //   44e021 46f01e 48d021 4ae020 1f701e 21501f 234022 25601f 275021 29601f 2b5021 4ce01a 4e8016 4fe01e
  //   60701f 51c01e 53a01d 55701d 57401e 59201d 5af01e 5cd01d 5ea01d
endmodule
