// Logisim project prav.circ as structural Verilog: 1 circuit, main circuit main
module main (
  input  [2:0] CO,
  output [19:0] _1i,
  output [19:0] _2i,
  output [19:0] _3i,
  output [19:0] _4i,
  output [19:0] _5i,
  output [19:0] _6i,
  output [19:0] _7i,
  output [19:0] _8i,
  output [19:0] _9i
);

  wire and_1_out, and_2_out, or_1_out, priority_encoder_1_out;
  wire [3:0] counter_1_q, counter_2_q;
  wire [19:0] multiplexer_1_out, rom_1_data, rom_2_data;

  and and_1 (and_1_out, CO[0], CO[1]);
  Priority_Encoder #(.select(1), .disabled(0)) priority_encoder_1 (
    .in0(CO[0]), .in1(CO[2]), .out(priority_encoder_1_out), .en_in(1'b1));  // open: gs, en_out
  Counter #(.width(4), .max('hc)) counter_1 (
    .count(1'b1), .Q(counter_1_q), .clk(and_2_out));  // open: load, D, carry, clr
  and and_2 (and_2_out, CO[2], CO[1]);
  Counter #(.width(4), .max('hc)) counter_2 (
    .count(1'b1), .Q(counter_2_q), .clk(and_1_out));  // open: load, D, carry, clr
  ROM #(.addrWidth(4), .dataWidth(20)) rom_1 (.addr(counter_2_q), .data(rom_1_data));  // open: sel
  ROM #(.addrWidth(4), .dataWidth(20)) rom_2 (.addr(counter_1_q), .data(rom_2_data));  // open: sel
  Multiplexer #(.width(20), .disabled(0), .enable("false")) multiplexer_1 (
    .in0(rom_1_data), .in1(rom_2_data), .out(multiplexer_1_out), .sel(priority_encoder_1_out));
  or or_1 (or_1_out, and_1_out, and_2_out);
  Register #(.width(20)) register_1 (.D(multiplexer_1_out), .en(1'b1), .Q(_1i), .clk(or_1_out));  // open: clr
  Register #(.width(20)) register_2 (.D(_1i), .en(1'b1), .Q(_2i), .clk(or_1_out));  // open: clr
  Register #(.width(20)) register_3 (.D(_2i), .en(1'b1), .Q(_3i), .clk(or_1_out));  // open: clr
  Register #(.width(20)) register_4 (.D(_3i), .en(1'b1), .Q(_4i), .clk(or_1_out));  // open: clr
  Register #(.width(20)) register_5 (.D(_4i), .en(1'b1), .Q(_5i), .clk(or_1_out));  // open: clr
  Register #(.width(20)) register_6 (.D(_5i), .en(1'b1), .Q(_6i), .clk(or_1_out));  // open: clr
  Register #(.width(20)) register_7 (.D(_6i), .en(1'b1), .Q(_7i), .clk(or_1_out));  // open: clr
  Register #(.width(20)) register_8 (.D(_7i), .en(1'b1), .Q(_8i), .clk(or_1_out));  // open: clr
  Register #(.width(20)) register_9 (.D(_8i), .en(1'b1), .Q(_9i), .clk(or_1_out));  // open: clr

  // Notes on the sheet:
  //   contents of rom_1 (hex, n*v repeats v):
  //   fc21f fd288 7d28f fd6aa f889f be1f f94a2 f909f 7462e
  //   contents of rom_2 (hex, n*v repeats v):
  //   7462e 7c27 387e0 f889f fd6e0 f9151 7d28f
endmodule
