// Logisim project proverka21.circ as structural Verilog: 1 circuit, main circuit proverkaChip21
module proverkaChip21 (
  input  C,
  input  in_2,
  input  [10:0] in_3,
  output [3:0] out_4,
  output out_5,
  output [15:0] out_6,
  output [15:0] out_7
);

  wire and_1_out, and_2_out, counter_1_carry, d_ff_1_q, d_ff_1_qn, not_1_out;
  wire [15:0] controlled_buffer_1_out, shift_register_1_q0;

  Counter #(.width(4), .max('hf), .ongoal("stay")) counter_1 (
    .count(C), .Q(out_4), .carry(counter_1_carry), .clk(C));  // open: load, D, clr
  not not_1 (not_1_out, C);
  and and_1 (and_1_out, counter_1_carry, not_1_out);
  D_Flip_Flop d_ff_1 (.clk(C), .D(and_1_out), .Q(d_ff_1_q), .Qn(d_ff_1_qn));  // open: preset, en, reset
  and and_2 (and_2_out, d_ff_1_qn, C);
  ROM #(.addrWidth(11), .dataWidth(16)) rom_1 (.addr(in_3), .data(out_6));  // open: sel
  Shift_Register #(.length(16)) shift_register_1 (
    .shift(1'b1), .in(in_2), .clk(and_2_out), .q0(shift_register_1_q0[0]), .q1(shift_register_1_q0[1]),
    .q2(shift_register_1_q0[2]), .q3(shift_register_1_q0[3]), .q4(shift_register_1_q0[4]),
    .q5(shift_register_1_q0[5]), .q6(shift_register_1_q0[6]), .q7(shift_register_1_q0[7]),
    .q8(shift_register_1_q0[8]), .q9(shift_register_1_q0[9]), .q10(shift_register_1_q0[10]),
    .q11(shift_register_1_q0[11]), .q12(shift_register_1_q0[12]), .q13(shift_register_1_q0[13]),
    .q14(shift_register_1_q0[14]), .q15(shift_register_1_q0[15]));  // open: out, load, clr, d0, d1, d2, d3, d4, d5, d6, d7, d8, d9, d10, d11, d12, d13, d14, d15
  assign controlled_buffer_1_out = d_ff_1_q ? out_6 : 16'bz;  // Controlled_Buffer controlled_buffer_1
  Comparator #(.width(16)) comparator_1 (
    .a(controlled_buffer_1_out), .b(shift_register_1_q0), .eq(out_5));  // open: gt, lt
  assign out_7 = shift_register_1_q0 ^ controlled_buffer_1_out;  // XOR_Gate xor_1, 16 bits wide

  // Notes on the sheet:
  //   Вход логической функции
  //    (Номер варианта - 1) как двоичное 10ти разрядное число
  //   contents of rom_1 (hex, n*v repeats v):
  //   9ecb afca ae2f 2df5 a71f 57ba dad9 ceae b6ea 75cd ed1d 9b6e 33f3 47e7 fc1d daf4 d1fc 7997 eccd c3bb
  //   cbb6 8b6f dec9 b6b9 eec9 35d7 6e6b d6ba d2cf 5ddc 273f fb1c 6b6d a977 f399 b6ad 5ebc e7d2 7acd 1eee
  //   8f9e e39e 6b2f 32fd 1fea cbcd 6ef8 f1d6 fce2 36eb e9b6 bcd6 fa35 79d9 8dee bf4a c577 f0bb 1ff8 a56f
  //   f4ad dfc4 b6cb 1fbc 85fe fe2c 26f7 afaa 3f95 e37a 8fb3 9db9 6bea b59b dcb9 e87b 8b3f 9f5c d675 7d4d
  //   574f c6de b3f4 cfb8 17f5 ba73 fc93 cb6b 6757 2efc ff60 da7c adb9 ae1f b3ce b6f8 e9ba 67f1 92ef fd58
  //   eee4 af2b ff06 9fe4 9ff 27b7 bb2d 59de 38fd c76e f9d4 6fd8 5e5e 87b7 f15b 697b d8f5 f2f8 3b2f e7a5
  //   7cad c57e 35ed 76b9 ad2f ccfc 9a7d c6ee 4ebd f27a 59db 52fd 4b7b 85fd b2fc 31fb 76b3 f16b e33d e774
  //   d4db 9be5 31fd ad3b 96eb a97e 617f 95dd c67d 6b9d faa5 d23f 9f9c f875 a79b 7cc7 675e eb2b 8df5 793b
  //   d7d2 e65b 6d76 1e5f 2cf7 d2ee 75bc dad5 1fe5 357d e95d 9cbe ae4f 79f1 afb4 673d cbe9 7e35 6f8b 4f5d
  //   17d7 c3cf ce75 768f f8ab 3d5d 7a3b 70df b9da eba9 bba6 ecd5 f237 ecd9 a79e a7dc ee87 fdc2 7e33 59e7
  //   cb79 bf2c d3dc cf78 d74b c9d7 775c 9eb3 fb38 2cef 6b79 fd64 9ed5 676d 1d6f eabc 89ef 73cd 5ee3 dd36
  //   ebe8 b97a 1afb fa3c e6ec e4ee 96e7 f6f bba5 3b57 cf56 fe32 79b3 f13b 69f9 6d79 1777 f1b5 6f99 1efc
  //   3ece 5af9 59bd a95f 2d7e 6d57 fe68 7697 add5 56eb 3f93 e9e6 b1f3 9af6 dc7a 7bc9 ad9b ea9d ed4e e8dd
  //   ba3e f2ba 5fd4 7aec afc9 edc6 db53 fac6 a7b3 4cfb b33b 7c9d d5d9 9fd8 375b 4cfd ee99 7e4d 7dc6 daf8
  //   5dad 7f16 a2bf 96bd df68 6e67 4ecf f2ad ce5b bd35 f6a9 39eb fd0b 7b5a 9c3f dcdc f14f f29b 73b9 7b9a
  //   f674 67e5 75e5 d0f7 b756 71bb 27f6 cf47 db39 b5d5 75b6 cd8f 755d 15fb bf58 fec8 a7cb 6e3b 2cbf bed2
  //   b49f 5dce 743f 757a 8d7b 4f7c dc37 ccdd c6f5 55e7 7796 69e7 f5f0 36bb a9f5 573e be36 e72d 713f 715f
  //   fa59 f4b5 6b75 5cfa 55de 875f eeca f693 dcb3 bcd3 e576 c5e7 acbd aeb9 85df 7b39 379d 8777 f94b d3f4
  //   47bd caaf c56f 65f3 639f fdd0 5f4d fc35 97d9 6dea 771b db99 b8bb 6df8 fd19 d9ad 957e a1bf 63d7 a5e7
  //   2ff8 74b7 57da bcf8 b58f f936 f2ae a3dd d557 bbd8 ba6e 2f79 acf3 2fce 4d7d cfa3 c73e 7ba9 9e76 33ed
  //   4f1f bc9d 3b37 db33 ed59 8bf9 b5cb fc66 f2f2 99cf eb59 f4b9 51f7 cd7c b2b7 6a77 f837 6dae 5eb5 eb3c
  //   fea8 ae6b 74eb 672f 7778 7a3d 27db b6d5 eba5 b96e 74af 73f2 37b5 bb87 be4d 2d7b 3f36 eab6 d65e df8a
  //   f3d4 47d7 fac9 c6db ea6d d73a f51e 75e6 b3ba 8fd5 d74d 3df1 f93c fc4e f89e b2fa cf5a d8dd ab2f a5bd
  //   8bb7 96db a3ed 2b6f 8b9f 79b6 7e72 f157 d6b5 54df e769 ad3e f38e bbb4 bd55 86fd 9b97 ed1e e477 4d7b
  //   57f8 7e9c 795d bb2e bcc7 ff6 eada b771 5e76 f36c a4ef 5dab 59eb 5797 dbe8 9dbc f696 d66d f31b f2cd
  //   379b 978f b99d f587 f38d fb86 c6f6 d36e f7e0 773c f734 b54f fe1c ddd2 8f3d db71 3dab 7fa4 34bf c53f
  //   1ebd 7ad3 ff42 727b 7b55 ab6e df89 a2fe eb2e ec37 f7a8 7a9b 34df bd1d 3a77 d9cd 73ab 89f7 6f53 5b8f
  //   71dd f63a b2f5 dec5 ef92 4b9f 1d3f 47eb 3dd6 e3ae 7b69 966f 7d3c 7b4b e25f 37a7 6faa 55cf 5bec 2f75
  //   6d1f 9e3d c977 daad 3fca 4b77 357b 4fd5 ef4a 4f6b cd67 4ddd 9d7a fb7 d8b7 c776 5cf3 c7c7 5776 8fad
  //   94df 3e75 76a7 22ff dd33 b5dc 5e6b 3de9 f3a6 c9dd c59f 5acf fe34 79ab 9eba 75e3 7dc9 173f 14ff df43
  //   a78f c9cf 6b57 25fd ebc3 eba3 d7a5 57ab d4fa 5bb9 2d5f fe52 8fb5 8ff8 76ae 6d3e b5ce 7b2d ef49 eeb8
  //   f58e fe45 6e3e a4fb e675 f953 39f3 f3d8 d1ed d5ae d6da 6e73 97b6 367e e5d3 5e97 9f4e ef8a f4e3 d8ed
  //   bdc6 d96b f43e 55db ead3 ab57 b36d f0e7 43bf 371f d6f1 cf96 7579 cfe4 b72d c9f6 5db6 b9ea 9dd9 7cdc
  //   bf86 56b7 4d6f fc1e fa95 769d 43fd d717 1fe6 6bd5 7eb2 2efa ccbb c5b7 7e56 e1de a73b 59af 659f a7d6
  //   9dcd e3ea bf52 ae97 96f5 f42f dae5 f9c9 d7a9 d99e c57b 786f e9f4 eac7 8cfb 9ead 83bf c6ed 667d ae5b
  //   9d97 dd3a f05f d1fa 335f 7ca7 b2db c5be a6fa e5a7 ee0f b5b6 bad9 49fe 57cb 517f f8ae d4f9 4bbd 5e9d
  //   cf4b 9f8d b0ef e3b3 e8cf d71b bed4 973d a72f 5cbb 6b5d f7b 76ba f4f4 3adb ba1f bc7c 755b 79e3 5fa3
  //   9fc6 b69d d27d dfd0 f0ee af5a fb07 e679 ec57 cdba 736d ae7c cdf4 f2d6 3bce f30f 72dd aed6 e7b1 e34f
  //   86df be17 bf45 6c7d 3b4f dcb6 fc59 f659 e1cf d56b ce1f 76ce d71e 8b7e b66d fb58 de4e b8fc a7ae f3aa
  //   ed6a 3b5d afa5 953f f0dd db1d 3db3 fc5c 1be7 7a57 3e9b f27c 79ad cf17 ec9d c1fe eeb1 cdd3 7f70 475f
  //   2f1f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
  //   Входной набор для функции со счетчика
  //   Результат оценки 1 - правильно
  //   Диагностика ошибок
endmodule
