// Logisim project proverka23.circ as structural Verilog: 1 circuit, main circuit proverka23
module proverka23 (
  input  [3:0] iData,
  input  C,
  input  [10:0] in_3,
  output SinhroOut,
  output Ok,
  output er,
  output [3:0] \напр ,
  output [3:0] \макс ,
  output [3:0] \шаг 
);

  wire and_1_out, comparator_1_eq, comparator_1_lt, comparator_2_eq, comparator_3_eq, comparator_4_eq,
       comparator_5_eq, comparator_6_eq, comparator_7_eq, comparator_8_eq, comparator_9_eq, comparator_10_eq,
       comparator_11_eq, comparator_12_eq, comparator_13_eq, comparator_14_eq, comparator_15_eq,
       comparator_16_eq, comparator_17_eq, or_2_out;
  wire [3:0] m0, m1, m2, m3, m4, m5, m6, m7, m8, m9, ma, mb, mc, md, me, mf, or_1_out, r0, r1, r2, r3, r4,
       r5, r6, r7, r8, r9, ra, rb, rc, rd, re, rf;
  wire [4:0] counter_1_q;

  and and_1 (and_1_out, C, ~comparator_1_eq);  // AND_Gate
  Counter #(.width(5), .max('h1f), .ongoal("stay"), .trigger("falling")) counter_1 (
    .count(1'b1), .Q(counter_1_q), .clk(and_1_out));  // open: load, D, carry, clr
  Comparator #(.width(5), .mode("unsigned")) comparator_1 (
    .a(counter_1_q), .b(5'b10001), .eq(comparator_1_eq), .lt(comparator_1_lt));  // open: gt
  cnta1 cnta1_1 (.in_1(in_3), .out_2({mf, me, md, mc, mb, ma, m9, m8}));
  cnta2 cnta2_1 (.in_1(in_3), .out_2({m7, m6, m5, m4, m3, m2, m1, m0}));
  cntmv cntmv_1 (.in_1(in_3), .out_2({\напр , \макс , \шаг }));
  and and_2 (SinhroOut, comparator_1_lt, C);
  // _16by4ShiftReg 16by4shiftreg_1: pin names not known; wires that end beside it: iData, 1'b1, SinhroOut, r0, r1, r2, r3, r4, r5, r6, r7, r8, r9, ra, rb, rc, rd, re, rf
  assign or_1_out = r0 | r1 | r2 | r3 | r4 | r5 | r6 | r7 | r8 | r9 | ra | rb | rc | rd | re | rf;  // OR_Gate or_1, 4 bits wide
  or or_2 (or_2_out, or_1_out[3], or_1_out[2], or_1_out[1], or_1_out[0]);
  Comparator #(.width(4), .mode("unsigned")) comparator_2 (.a(r0), .b(m0), .eq(comparator_2_eq));  // open: gt, lt
  Comparator #(.width(4), .mode("unsigned")) comparator_3 (.a(r1), .b(m1), .eq(comparator_3_eq));  // open: gt, lt
  Comparator #(.width(4), .mode("unsigned")) comparator_4 (.a(r2), .b(m2), .eq(comparator_4_eq));  // open: gt, lt
  Comparator #(.width(4), .mode("unsigned")) comparator_5 (.a(r3), .b(m3), .eq(comparator_5_eq));  // open: gt, lt
  Comparator #(.width(4), .mode("unsigned")) comparator_6 (.a(r4), .b(m4), .eq(comparator_6_eq));  // open: gt, lt
  Comparator #(.width(4), .mode("unsigned")) comparator_7 (.a(r5), .b(m5), .eq(comparator_7_eq));  // open: gt, lt
  Comparator #(.width(4), .mode("unsigned")) comparator_8 (.a(r6), .b(m6), .eq(comparator_8_eq));  // open: gt, lt
  Comparator #(.width(4), .mode("unsigned")) comparator_9 (.a(r7), .b(m7), .eq(comparator_9_eq));  // open: gt, lt
  Comparator #(.width(4), .mode("unsigned")) comparator_10 (.a(r8), .b(m8), .eq(comparator_10_eq));  // open: gt, lt
  Comparator #(.width(4), .mode("unsigned")) comparator_11 (.a(r9), .b(m9), .eq(comparator_11_eq));  // open: gt, lt
  Comparator #(.width(4), .mode("unsigned")) comparator_12 (.a(ra), .b(ma), .eq(comparator_12_eq));  // open: gt, lt
  Comparator #(.width(4), .mode("unsigned")) comparator_13 (.a(rb), .b(mb), .eq(comparator_13_eq));  // open: gt, lt
  Comparator #(.width(4), .mode("unsigned")) comparator_14 (.a(rc), .b(mc), .eq(comparator_14_eq));  // open: gt, lt
  Comparator #(.width(4), .mode("unsigned")) comparator_15 (.a(rd), .b(md), .eq(comparator_15_eq));  // open: gt, lt
  Comparator #(.width(4), .mode("unsigned")) comparator_16 (.a(re), .b(me), .eq(comparator_16_eq));  // open: gt, lt
  Comparator #(.width(4), .mode("unsigned")) comparator_17 (.a(rf), .b(mf), .eq(comparator_17_eq));  // open: gt, lt
  and and_3 (Ok, comparator_2_eq, comparator_3_eq, comparator_4_eq, comparator_5_eq, comparator_6_eq, comparator_7_eq, comparator_8_eq, comparator_9_eq, comparator_10_eq, comparator_11_eq, comparator_12_eq, comparator_13_eq, comparator_14_eq, comparator_15_eq, comparator_16_eq, comparator_17_eq);
  and and_4 (er, ~Ok, comparator_1_eq, or_2_out);  // AND_Gate

  // Notes on the sheet:
  //   вариант
endmodule
