// Logisim project stnMem1.circ as structural Verilog: 1 circuit, main circuit stnMem1
module stnMem1 (
  input  [10:0] in_1,
  output [31:0] out_2
);

  ROM #(.addrWidth(11), .dataWidth(32)) rom_1 (.addr(in_1), .data(out_2));  // open: sel

  // Notes on the sheet:
  //   contents of rom_1 (hex, n*v repeats v):
  //   d11014 b2cb2cb0 b2cb2cb2 b2cb2cb2 b2cb2cb0 b0438c05 b2cb2cb0 b2cb2cb2 b2cb2c28 b2cb2c28 b2cb0a38
  //   b2cb2c28 b2cb2cb2 b2cb2cb0 b2cb2c30 b2cb2cb0 b2cb0f01 b2cb2c40 b2cb1100 b2cb1101 b2cb2cb1 b2cb2cb2
  //   b2cb0101 b2cb2cb2 b2cb2cb2 b0a00fb0 b2cb2cb0 b2cb2cb0 35340c01 b2cb2cb2 b2c44041 44840e18 54eb0d7d
  //   b2cb0034 b2cb2c04 b2cb2cb0 b2cb2cb0 b2cb2c05 b2c08540 b2cb0338 b2cb2cb0 b2cb2c0d b0509148 b2cb2cb2
  //   b2cb2cb0 b2cb2cb0 b2cb2cb0 b2cb2cb2 b2cb2cb2 b2cb2cb0 b2cb2cb2 b2cb2cb2 b2cb2c3c b2cb2cb1 b2cb2cb1
  //   b2c44010 b2cb2cb1 b2cb2c44 b2cb2cb1 b2cb2cb2 b2cb2cb2 b2cb2cb1 b2cb2c61 b2cb1914 b2c00d48 b2cb0100
  //   b2cb2c05 b2cb2c08 b2cb2c08 b2c08e2c 4*b2cb2cb2 b2cb0a38 b2cb2cb2 b2cb2c2c b2cb2cb2 b2cb2cb0 b2cb2cb2
  //   b2cb0e0c b2cb2cb2 b2cb2cb1 b2cb2cb2 b2cb2cb1 b2cb2c48 b2cb2cb1 b2cb2cb1 b2cb1715 b2cb2cb2 b2cb2cb2
  //   b2cb2c30 b2cb2cb2 b2cb002c b2cb2cb2 b2cb2cb2 b2cb2cb0 b2cb2cb0 b2cb0844 b2cb2cb0 b2cb2cb0 b2cb2c28
  //   b2cb2cb2 b2cb2c29 b2cb2cb2 b2cb2cb0 b2cb2cb2 b2cb2cb0 b2cb2cb0 b2cb0f01 b2cb2cb2 b2cb2cb1 b2cb2cb2
  //   b2cb2cb2 b2cb2c49 b2cb2cb2 b2cb2c50 b2c5082c 4*b2cb2cb2 b2cb1815 b2cb2cb0 b2cb002d b004112c b2cb2cb2
  //   b2cb2cb0 b2cb2cb0 b2cb0238 b2cb2c0c b2cb2cb2 b2cb2c0c b2cb0414 b2cb2c10 b2cb2c1c b2cb2c29 b2cb2c29
  //   b2cb2c2c b2cb2cb2 b2cb2cb0 b2cb2cb2 b2cb2cb0 b2cb2cb2 b2cb1001 b2cb2cb1 b2cb1101 b2cb1120 b2cb2cb2
  //   b2cb2cb2 b2cb2c60 b2cb2c60 b2cb2cb2 b2cb002c b2cb2c00 b2cb0101 b2cb2c04 b2c08834 b2cb2cb2 b2cb0414
  //   b2cb2cb2 b2cb2c1c b2cb2cb0 b2cb0a21 b2cb2cb0 b2cb2cb0 b2cb0a41 b2cb0a4c b2cb0a4c b2cb0a54 b2cb2cb2
  //   b2cb2c30 b2cb2c3c b0f15148 b2cb2cb0 b2cb2cb2 b2cb2c3d b2cb2cb0 b2cb2c44 b2cb2cb2 b2cb2cb1 b2cb2c54
  //   b2cb2cb2 b2cb2c00 b2cb2cb0 b2cb2c08 b2cb2cb2 b2cb2c0c b2cb2cb0 b2cb2c0d b2cb2cb0 b2cb2cb2 b2cb0701
  //   b080c030 b2cb2cb2 b2cb0a38 b2cb2c28 b2cb0a4c b2cb2cb0 b2cb2c31 35340c4d b2cb2c3c b2cb2cb0 b2cb2c3d
  //   b2cb2cb2 b2cb2cb1 b2cb2c44 b2cb2c44 b2cb2c49 b1401055 b2cb2cb1 b2cb2cb1 b2cb2cb2 b2cb2c04 b2cb0141
  //   b2cb2cb2 b2cb2c0c b2cb2cb0 b2cb2cb0 b2cb2cb2 b2cb2cb2 b2cb2cb2 b2cb2c19 b2cb2c28 b2cb0a20 b2cb2c28
  //   b2cb2cb2 b2cb2cb0 b2cb2cb2 b2cb2c28 b2cb2cb0 b2cb2cb0 b2cb2cb0 b2cb2c30 b2cb2c30 b2cb2c34 b2cb0f38
  //   b2c3d039 b2c44034 b2cb2cb2 b2c4532c b2cb2cb2 b2cb2cb0 b2cb2cb2 b2cb2cb0 b2cb2cb0 b2cb2cb0 b2cb2cb2
  //   b2cb2cb0 b2cb2cb2 b2cb0418 b2cb2c11 b2cb0700 b2cb2cb2 b2cb0a01 b0a01008 b2c29311 b2cb2cb0 b2cb2cb0
  //   3481c031 b2c39038 b0f38438 b2cb2cb1 b2cb2cb2 b2cb1120 b2cb2cb1 b2cb2cb1 b2cb1278 b2cb2cb2 b2c54025
  //   b2cb2cb1 b2cb0028 b2cb2cb0 b2c08809 b2cb2cb2 b040022c b2cb2cb0 b2cb0620 b2cb2c1c b2cb2c20 b2cb2cb0
  //   b2cb0a01 b2cb0a38 b2cb2cb0 28e35148 b2cb2c29 b2cb2cb0 b2cb2cb2 b2cb2cb0 b2cb2c30 b2cb2c30 b2cb2c30
  //   b2cb2cb2 b2cb2c39 b2cb2c44 b2cb1138 b2cb2c44 b2c45239 b2cb2cb2 b2cb2cb2 b2cb2cb1 b2cb2cb0 b2cb2c04
  //   b2cb2cb2 b2cb2c0c b2cb2cb2 b2cb2c15 b2cb2c28 b2cb2c28 b2cb2c28 b2cb2cb0 b2c29020 b2cb2c29 b2cb0a4c
  //   b2cb2cb2 b2cb0b14 b2cb2cb2 b2cb2cb2 b2cb0d00 b2cb2cb0 b2cb2c44 b2cb2cb2 b2cb2c44 b2cb2cb1 b2cb2cb1
  //   b2cb2c50 b2cb2c54 b2cb2cb1 b2cb2cb2 b2cb2cb2 b2cb2cb0 b2cb000c b2cb2c00 b2cb2cb0 b0115144 b2cb2cb0
  //   b2cb2cb0 b2cb2cb0 b2cb2cb2 b2cb2c10 b2cb2cb0 b2cb2cb2 b2cb2cb2 b2cb2cb2 b2cb2cb1 b2cb2c45 b2cb2cb1
  //   b2c7ca4c b2cb2cb0 b2cb2cb0 b2cb2c30 b2cb2cb0 b2cb2cb2 38b38238 b2cb2cb2 b2c3d33d b2cb2c40 b2cb2c40
  //   b2cb2cb2 b2cb2c41 b2cb2cb1 6*b2cb2cb2 b2cb2c28 b2cb2cb2 b2cb2cb0 b2cb2cb2 b2cb2c2c b2cb2cb0 b2cb2cb2
  //   b2cb2cb0 b2cb2cb0 b2cb2cb2 b2cb2cb0 b2cb0d38 4*b2cb2cb2 b2cb2c44 b2cb2cb1 44e2ce30 b2cb2cb2 b2cb2cb2
  //   b2cb2cb2 b2cb2c61 b2cb2cb1 b2cb2cb0 b2cb000c b2cb2cb2 b2cb2cb0 b2c0402c b0101000 b2cb2cb2 b2cb2cb0
  //   b2cb2cb2 b2cb2cb0 b2cb2cb2 b2cb2cb0 b2cb2c29 b2cb2cb0 b2cb2cb2 b2c30028 b2cb2cb0 b2cb2c34 b2cb2cb2
  //   b2cb2cb2 b2cb0f00 b2cb2cb0 b2cb2c3c 3ce11a7c b2cb2c44 b2cb2cb2 b2cb2cb1 b2cb2c55 b1800954 b2cb2cb2
  //   b2cb2cb1 b2cb1821 b2cb2cb2 b2cb2c00 b2cb0100 b2cb2cb0 b2cb2cb2 b2cb2cb2 b2cb2cb0 b2cb2cb2 b2cb0600
  //   b2cb2cb0 b2cb0a00 b2cb2c28 b2cb2cb0 b2cb2cb0 b2cb2cb0 b2cb2c3c b2cb2cb2 b2cb2cb1 b2cb2c44 b2cb2cb1
  //   b2cb2cb2 b2cb2c00 4*b2cb2cb0 b2cb0114 b2cb0300 b2cb0700 b2cb2c28 b2cb2cb2 b2cb2c28 b2cb2cb2 b2cb2cb2
  //   b2cb2cb0 2c508034 b2cb2c2c b2cb2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
endmodule
