// Logisim project stnMem2.circ as structural Verilog: 1 circuit, main circuit stnMem2
module stnMem2 (
  input  [10:0] in_1,
  output [31:0] out_2
);

  ROM #(.addrWidth(11), .dataWidth(32)) rom_1 (.addr(in_1), .data(out_2));  // open: sel

  // Notes on the sheet:
  //   contents of rom_1 (hex, n*v repeats v):
  //   95c828e0 3523982 c04510d3 c05020a1 14cb6d71 38244a2 a00c6d82 c2804801 b20c14d2 e24c2171 b39220b3
  //   e45220a3 c2c53d82 b78120c3 e40300b1 c3903873 820d44a2 614244a2 c3892ce0 4d500d3 538c14d2 c60a3847
  //   53844d03 c04e04e1 c0d02182 200db153 a4c40181 c1501443 530048e0 c4131c81 bb080ce4 810420d1 2b0a5403
  //   44087cd3 454042 100a6051 101000d3 340008b1 56400c83 b4c13822 33907d71 32c53563 80cd1450 cb0714d3
  //   a41e28e0 a4cb1583 a4cb7c12 c2ce0472 c2d348a3 c00b6c32 cb2c34e1 c3c008b3 4455cd6 20d5c83 38c00d3
  //   e08d20a3 101438d3 51038d3 114c14d3 c48e34a2 c5c540d6 74cc0401 360c00d3 c14b20d2 83c534a3 d49e28e0
  //   340414b1 4482dc1 4482dc1 e11714d2 c0c04182 c0ce4010 cb044d13 c28030d1 d1100183 c2c50451 538d49c1
  //   cb0b7d53 c39270a2 c3455821 d7cd3822 c3c83574 38478a3 c4454051 13914cd3 831714d2 41444cb3 414478a3
  //   35b60e0 c0094881 cb0a3923 a4124cc7 c3132ce1 52911450 cb0100a2 c0404042 338b70d1 33901051 25714d2
  //   a38c0103 a38f6cb3 e48534a3 c29078a3 305b60a2 c2c03d83 b1411441 c2c51cd3 b38100d3 c00a2050 c38d3
  //   c3c54903 4d400d3 c4400972 cb1120b2 21438d3 cb2c4d04 510e4451 83cf14d2 c54e0903 cb1600f2 c5c01083
  //   c5c84523 148028e0 29114d3 c4984cb1 3402c81 c0110012 101100d3 14c46ca2 43820123 9020a3 c0c524a1
  //   b7cd14d2 34854050 e2cc0123 10e3561 20214d2 348534a3 4804931 cb0b4cd1 b6d114d2 c3451010 d20a4cb2
  //   c3d35ca3 144a0073 39200d3 48044e0 12107ca3 cb124d72 cb2c6020 52cf00a3 545200a3 c60e2884 52911450
  //   c04858a0 549b3872 51d30cb6 e0d00043 c0d02182 d21114d2 c1433903 52df2883 a08044e0 21714d2 a3901472
  //   a39120d3 f5524cd3 770d20a3 b21714d2 34400a1 cb0c0074 834028e0 2c534e0 540d20a3 f15920a3 cb0f38f3
  //   3953903 f49360a2 215010b2 c44e30e0 278d7c50 2c828e0 c5c840a3 d1101450 238b0c83 e40200d2 cb0338d1
  //   e4014cd3 34050963 2040113 400d20b3 cb064ca3 501014d2 115011b1 cb2cb0a2 200b14d2 e5c534a3 441f0961
  //   b0070101 340009c1 500c1523 54904cd2 f2174c32 20b14f2 c3d03982 38700d3 852dc1 b14f4d52 4d82883
  //   348420d3 420b0123 83000d02 c04040a3 540544d1 b1c300b3 c09f1ca3 e40100d3 34080403 40026c43 cb047863
  //   c15060e0 cb062103 340008b1 4120183 b7042183 841e60a2 c28d7c71 a3870174 c28e1cb3 e40e48a3 a39220a3
  //   a40530d1 a4c770c2 3441881 840e34e0 52900113 710d7ca3 39714d2 30041881 c4403d03 524c00d3 cb126d82
  //   3444051 c0537cd3 300b00d2 300d6083 339060a3 c0d038c3 408e4163 cb0414c2 3c10103 30503822 14d011f1
  //   c2802c83 f1523 44040d6 7c25850 c01538d2 c3884451 348420d3 d38244a0 f41b0c83 220b3 c41b54b3 25c534a3
  //   130840d3 14d020d3 a0022883 cb1438c2 4cb2c83 815500d2 830534a3 4520153 238d14d2 c0d31001 54810050
  //   44c40101 b70d20a3 900062 234858a0 818c7ca3 d1051 b6d82883 a38c0103 35220d3 4cf20d2 b00f4850 cb0b38c3
  //   c00a0103 4127983 5051073 854024b3 cb2cb2c3 138244a0 834a1422 b38c0122 e48d20a3 38614d2 cb180103
  //   c6050963 820a00b3 100b14d2 544c14d3 cb024cb7 44f0107 cb033834 39814d2 2934083 5c034e0 61200d3
  //   a3910101 23981450 31cd1563 b01714d3 cb0b14c1 f2111450 c2db3442 c3086083 701014d2 f4d058c0 40a2117
  //   cb110142 a3844801 138138b1 41443903 539400d3 40504e0 66c300d3 c61330d6 c6134181 f1570032 50e34a2
  //   d21120c3 101000d3 c15048d6 14d01001 30041881 31505850 c0c804e0 8b0123 540c00a3 c2900021 cb0b4ca2
  //   cb0b6d13 130840a2 340e1432 41443903 138244a2 834e7d23 a01020c3 51021441 c4c714d1 c3401c84 304e2450
  //   c39120f3 334e0912 1060013 54c0123 c40e6001 345200c3 50091004 cb153803 c0452df1 cb2c0d34 cb0414b3
  //   c1c21501 c20200d3 5553903 cb2cb0a2 a2107982 c28b20c3 40838d3 b14f1552 cb0b7cc2 c00a4d82 c21914d2
  //   c3131c01 d20a4cb2 239114b3 c3c53472 c3ce4523 cb0f7d23 cb2cb104 30e60a2 10101422 534d20a3 c48e3d72
  //   c51038b3 c5c04d13 340528e0 f31920a3 f1570032 10600d3 cb2cb2c0 4003c81 5340a2 d38244a2 c0452df1
  //   120b00b3 cb0320b1 33907c50 c18858a2 a38d0101 31cd1563 a4c770c2 c2ce04a3 e08558a0 c14b70d2 4cc14d2
  //   cb0d0d31 cb2cb0f0 b7cd6d72 f0184801 e08040d2 12ce3512 e2c40123 c4804033 40104cc1 344d4cb2 848420d3
  //   cb2c6021 814f14b1 50852c81 c14320c7 b14a4451 720b1422 121078a3 c0506c63 c0c04001 400d20b7 c15000d2
  //   120d44a2 701014c0 700d44a2 e45214d2 c00a0103 c20d0117 c3903873 b01238d3 cb110881 130840d3 d2032101
  //   134848a2 c6001081 11132cb2 900153 29114d3 35220f2 101000d3 b38338b3 24082dc1 840114a3 1c028e0
  //   c28040f3 40f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
endmodule
